# Fritzing sketch Powermeter (saved by Fritzing 1.0.2b)
breadboards: 1

parts:
  OLED_I2C1 = OLED 128x64 I2C Monochrome Display
  INA1 = INA219 DC Current Sensor Breakout
  J1 = Camdenboss CTB0158-2 [part_number=CTB0158-2 package=THT]
  LED1 = smd LED [color="Red (633nm)" package="1206 [SMD]"]
  R1 = Resistor [tolerance=±5% power=0.25W resistance=220 package=THT]
  Part1 = Arduino Uno (Rev3) - ICSP
  D1 = SOLAR-IXYS [package=solarbit-12x1]

nets:
  N1: OLED_I2C1.SDA, INA1.SDA, Part1.A4/SDA
  N2: OLED_I2C1.SCK, INA1.SCL, Part1.A5/SCL
  VDD: OLED_I2C1.VDD, INA1.VCC, Part1.5V
  GND: OLED_I2C1.GND, INA1.GND, J1.pin1, R1.Pin_1, Part1.GND
  N3: INA1.Vin+2, D1.A
  N4: J1.terminal_1, D1.C
  N5: LED1.cathode, R1.Pin_0

custom parts:
  INA219 DC Current Sensor Breakout: INA DC Current Sensor Breakout
